// Logisim project Atividade1.1.circ as structural Verilog: 1 circuit, main circuit main
module main (
  input  A,
  input  B,
  input  C,
  input  d_0,
  input  d_1,
  input  d_2,
  input  d_3,
  input  d_4,
  input  d_5,
  input  d_6,
  input  d_7,
  output q
);

  wire and_1_out, and_2_out, and_3_out, and_4_out, and_5_out, and_6_out, and_7_out, and_8_out, not_1_out,
       not_2_out, not_3_out;

  not not_1 (not_1_out, A);
  not not_2 (not_2_out, B);
  not not_3 (not_3_out, C);
  and and_1 (and_1_out, d_0, not_1_out, not_2_out, not_3_out);
  and and_2 (and_2_out, d_1, not_1_out, not_2_out, C);
  and and_3 (and_3_out, d_2, not_1_out, B, not_3_out);
  and and_4 (and_4_out, d_3, not_1_out, B, C);
  and and_5 (and_5_out, d_4, A, not_2_out, not_3_out);
  and and_6 (and_6_out, d_5, A, not_2_out, C);
  and and_7 (and_7_out, d_6, A, B, not_3_out);
  and and_8 (and_8_out, d_7, A, B, C);
  or or_1 (q, and_1_out, and_2_out, and_3_out, and_4_out, and_5_out, and_6_out, and_7_out, and_8_out);
endmodule
