// Logisim project Atividade1.2.circ as structural Verilog: 1 circuit, main circuit main
module main (
  input  I0,
  input  I1,
  input  I2,
  input  I3,
  input  I4,
  input  I5,
  input  Carga
);

  wire and_1_out, and_2_out, and_3_out, and_4_out, and_5_out, and_6_out, and_7_out, and_8_out, and_9_out,
       and_10_out, and_11_out, and_12_out, clock_1_out, d_ff_1_q, d_ff_2_q, d_ff_3_q, d_ff_4_q, d_ff_5_q,
       d_ff_6_q, not_1_out, or_1_out, or_2_out, or_3_out, or_4_out, or_5_out, or_6_out, undriven;

  and and_1 (and_1_out, Carga, I0);
  and and_2 (and_2_out, not_1_out, d_ff_1_q);
  or or_1 (or_1_out, and_1_out, and_2_out);
  Clock clock_1 (.out(clock_1_out));
  D_Flip_Flop d_ff_1 (.clk(clock_1_out), .D(or_1_out), .Q(d_ff_1_q));  // open: Qn, preset, en, reset
  LED A0 (.in(d_ff_1_q));
  and and_3 (and_3_out, Carga, I1);
  or or_2 (or_2_out, and_3_out, and_4_out);
  and and_4 (and_4_out, not_1_out, d_ff_2_q);
  D_Flip_Flop d_ff_2 (.clk(clock_1_out), .D(or_2_out), .Q(d_ff_2_q));  // open: Qn, preset, en, reset
  LED A1 (.in(d_ff_2_q));
  and and_5 (and_5_out, Carga, I2);
  or or_3 (or_3_out, and_5_out, and_6_out);
  and and_6 (and_6_out, not_1_out, d_ff_3_q);
  D_Flip_Flop d_ff_3 (
    .clk(clock_1_out), .D(or_3_out), .Q(d_ff_3_q), .en(undriven), .reset(undriven));  // open: Qn, preset
  LED A2 (.in(d_ff_3_q));
  and and_7 (and_7_out, Carga, I3);
  or or_4 (or_4_out, and_7_out, and_8_out);
  and and_8 (and_8_out, not_1_out, d_ff_4_q);
  D_Flip_Flop d_ff_4 (.clk(clock_1_out), .D(or_4_out), .Q(d_ff_4_q));  // open: Qn, preset, en, reset
  LED A3 (.in(d_ff_4_q));
  and and_9 (and_9_out, Carga, I4);
  and and_10 (and_10_out, not_1_out, d_ff_5_q);
  or or_5 (or_5_out, and_9_out, and_10_out);
  D_Flip_Flop d_ff_5 (.clk(clock_1_out), .D(or_5_out), .Q(d_ff_5_q));  // open: Qn, preset, en, reset
  and and_11 (and_11_out, Carga, I5);
  LED A4 (.in(d_ff_5_q));
  and and_12 (and_12_out, not_1_out, d_ff_6_q);
  or or_6 (or_6_out, and_11_out, and_12_out);
  not not_1 (not_1_out, Carga);
  D_Flip_Flop d_ff_6 (.clk(clock_1_out), .D(or_6_out), .Q(d_ff_6_q));  // open: Qn, preset, en, reset
  LED A5 (.in(d_ff_6_q));
endmodule
