// Logisim project ex5.circ as structural Verilog: 1 circuit, main circuit main
module main (
  input  A3,
  input  A2,
  input  A1,
  input  A0,
  input  B3,
  input  B2,
  input  B1,
  input  B0,
  input  OR,
  input  AND,
  input  NOT
);

  wire and_1_out, and_2_out, and_3_out, and_4_out, and_5_out, and_6_out, and_7_out, and_8_out, and_9_out,
       and_10_out, and_11_out, and_12_out, and_13_out, and_14_out, and_15_out, and_16_out, not_1_out,
       not_2_out, not_3_out, not_4_out, or_1_out, or_2_out, or_3_out, or_4_out, or_5_out, or_6_out, or_7_out,
       or_8_out;

  not not_1 (not_1_out, A3);
  and and_1 (and_1_out, not_1_out, NOT);
  not not_2 (not_2_out, A2);
  and and_2 (and_2_out, not_2_out, NOT);
  not not_3 (not_3_out, A1);
  and and_3 (and_3_out, not_3_out, NOT);
  not not_4 (not_4_out, A0);
  and and_4 (and_4_out, A3, B3);
  and and_5 (and_5_out, not_4_out, NOT);
  and and_6 (and_6_out, A2, B2);
  and and_7 (and_7_out, and_6_out, AND);
  and and_8 (and_8_out, and_4_out, AND);
  and and_9 (and_9_out, A1, B1);
  and and_10 (and_10_out, and_9_out, AND);
  and and_11 (and_11_out, A0, B0);
  and and_12 (and_12_out, and_11_out, AND);
  or or_1 (or_1_out, A2, B2);
  or or_2 (or_2_out, A3, B3);
  and and_13 (and_13_out, or_2_out, OR);
  and and_14 (and_14_out, or_1_out, OR);
  or or_3 (or_3_out, A1, B1);
  and and_15 (and_15_out, or_3_out, OR);
  or or_4 (or_4_out, A0, B0);
  and and_16 (and_16_out, or_4_out, OR);
  or or_5 (or_5_out, and_16_out, and_12_out, and_5_out);
  or or_6 (or_6_out, and_15_out, and_10_out, and_3_out);
  or or_7 (or_7_out, and_14_out, and_7_out, and_2_out);
  or or_8 (or_8_out, and_13_out, and_8_out, and_1_out);
  LED C3 (.in(or_8_out));
  LED C2 (.in(or_7_out));
  LED C0 (.in(or_5_out));
  LED C1 (.in(or_6_out));
endmodule
