// Logisim project Atividade1.3.circ as structural Verilog: 1 circuit, main circuit main
module main (
  input  Entrada_de_Dados
);

  wire clock_1_out, d_ff_1_q, d_ff_2_q, d_ff_3_q, d_ff_4_q, d_ff_5_q, d_ff_6_q;

  Clock clock_1 (.out(clock_1_out));
  D_Flip_Flop d_ff_1 (.clk(clock_1_out), .D(Entrada_de_Dados), .Q(d_ff_1_q));  // open: Qn, preset, en, reset
  LED D5 (.in(d_ff_1_q));
  D_Flip_Flop d_ff_2 (.clk(clock_1_out), .D(d_ff_1_q), .Q(d_ff_2_q));  // open: Qn, preset, en, reset
  LED D4 (.in(d_ff_2_q));
  D_Flip_Flop d_ff_3 (.clk(clock_1_out), .D(d_ff_2_q), .Q(d_ff_3_q));  // open: Qn, preset, en, reset
  LED D3 (.in(d_ff_3_q));
  D_Flip_Flop d_ff_4 (.clk(clock_1_out), .D(d_ff_3_q), .Q(d_ff_4_q));  // open: Qn, preset, en, reset
  LED D2 (.in(d_ff_4_q));
  D_Flip_Flop d_ff_5 (.clk(clock_1_out), .D(d_ff_4_q), .Q(d_ff_5_q));  // open: Qn, preset, en, reset
  LED D1 (.in(d_ff_5_q));
  D_Flip_Flop d_ff_6 (.clk(clock_1_out), .D(d_ff_5_q), .Q(d_ff_6_q));  // open: Qn, preset, en, reset
  LED D0 (.in(d_ff_6_q));
endmodule
