// Logisim project ex4.circ as structural Verilog: 1 circuit, main circuit main
module main (
  input  X0,
  input  X1,
  input  X2,
  input  X3,
  input  Y0,
  input  Y1,
  input  Y2,
  input  Y3,
  input  ADD,
  input  SUB,
  output OVERFLOW,
  output CARRY,
  output S0,
  output S1,
  output S2,
  output S3
);

  wire adder_2_cout, adder_3_cout, adder_4_cout, and_1_out, and_2_out, and_3_out, and_4_out, and_5_out,
       and_6_out, and_7_out, and_8_out, or_1_out, or_2_out, or_3_out, or_4_out;

  xor xor_1 (OVERFLOW, CARRY, adder_2_cout);
  and and_1 (and_1_out, ~Y0, SUB);  // AND_Gate
  and and_2 (and_2_out, Y0, ADD);
  or or_1 (or_1_out, and_2_out, and_1_out);
  and and_3 (and_3_out, Y1, ADD);
  or or_2 (or_2_out, and_3_out, and_5_out);
  Adder #(.width(1)) adder_1 (.a(or_1_out), .b(X0), .out(S0), .cin(adder_2_cout), .cout(CARRY));
  and and_4 (and_4_out, Y2, ADD);
  and and_5 (and_5_out, ~Y1, SUB);  // AND_Gate
  Adder #(.width(1)) adder_2 (.a(or_2_out), .b(X1), .out(S1), .cin(adder_3_cout), .cout(adder_2_cout));
  and and_6 (and_6_out, ~Y2, SUB);  // AND_Gate
  or or_3 (or_3_out, and_4_out, and_6_out);
  Adder #(.width(1)) adder_3 (.a(or_3_out), .b(X2), .out(S2), .cin(adder_4_cout), .cout(adder_3_cout));
  and and_7 (and_7_out, ~Y3, SUB);  // AND_Gate
  and and_8 (and_8_out, Y3, ADD);
  or or_4 (or_4_out, and_8_out, and_7_out);
  Adder #(.width(1)) adder_4 (.a(or_4_out), .b(X3), .out(S3), .cin(SUB), .cout(adder_4_cout));
endmodule
